// Logisim project 1mb_16kb_decode.circ as structural Verilog: 1 circuit, main circuit main
module main (
  input  A19,
  input  A18,
  input  A17,
  input  A16,
  input  A15,
  input  A14,
  input  A13,
  input  IO_not_M,
  input  not_RD,
  input  not_WR,
  input  not_DEN,
  input  not_EN
);

  wire nand_1_out, nand_2_out, nand_3_out, nand_4_out, nand_5_out, not_1_out, not_2_out, not_3_out,
       not_4_out, not_5_out, or_1_out, or_2_out, or_3_out, or_4_out;

  nand nand_1 (nand_1_out, 1'b1, 1'b1, A19, A18, A17, A16, A15, A14);
  not not_1 (not_1_out, not_DEN);
  not not_2 (not_2_out, nand_1_out);
  not not_3 (not_3_out, A13);
  not not_4 (not_4_out, IO_not_M);
  not not_5 (not_5_out, IO_not_M);
  nand nand_2 (nand_2_out, not_1_out, not_EN);
  nand nand_3 (nand_3_out, A19, nand_1_out);
  LED SRAM (.in(nand_3_out));
  nand nand_4 (nand_4_out, not_2_out, not_3_out);
  LED ROM1 (.in(nand_4_out));
  nand nand_5 (nand_5_out, not_2_out, A13);
  LED ROM2 (.in(nand_5_out));
  or or_1 (or_1_out, IO_not_M, not_RD);
  LED not_MEMR (.in(or_1_out));
  or or_2 (or_2_out, IO_not_M, not_WR);
  LED not_MEMW (.in(or_2_out));
  or or_3 (or_3_out, not_4_out, not_RD);
  LED not_IOR (.in(or_3_out));
  or or_4 (or_4_out, not_5_out, not_WR);
  LED not_IOW (.in(or_4_out));
  LED not_CE (.in(nand_2_out));
endmodule
